# Fritzing sketch Train collosion avoiding system (saved by Fritzing 0.9.4)
breadboards: 1

parts:
  Part1 = Arduino Uno (Rev3)
  LED1 = LEDs [package=led10mm]
  LED2 = LEDs [package=led10mm]
  LED3 = LEDs [package=led10mm]
  M1 = fc-51 [package=THT]
  M2 = fc-51 [package=THT]
  M3 = fc-51 [package=THT]
  M4 = fc-51 [package=THT]
  LCD1 = LCD screen  # not connected
  J1 = Dagu DGServo 9g header (male) [package=THT]
  J2 = Dagu DGServo 9g header (male) [package=THT]
  J3 = Basic Servo

nets:
  N1: Part1.A4/SDA, J1.gnd
  N2: Part1.A5/SCL, J2.gnd
  N3: Part1.D9_PWM, M2.pin1
  N4: Part1.D10_PWM/SS, J3.pulse
  N5: Part1.D2, M1.pin1
  N6: Part1.D3_PWM, M4.pin1
  N7: Part1.D4, M3.pin1
  N8: LED1.C, LED2.C, LED3.C, J1.pulse, J3.gnd
  N9: M1.pin2, M2.pin2, M3.pin2
  VCC: M1.pin3, M2.pin3, M3.pin3, M4.pin2, M4.pin3, J1.Vcc, J3.vcc
